# Fritzing sketch CityLab_Festival2024 (saved by Fritzing 0.9.3b)
breadboards: 3

parts:
  Part1 = Arduino Mega 2560 (Rev3)
  LCD1 = LCD screen
  R1 = Rotary Potentiometer (Small) [maximum_resistance=100kΩ package=THT]
  LCD2 = LCD screen
  R2 = Resistor [tolerance=±5% resistance=220 package=THT]
  R3 = Rotary Potentiometer (Small) [maximum_resistance=100kΩ package=THT]
  SPKR1 = Loudspeaker
  RHT1 = Humidity and Temperature Sensor RHT03

nets:
  N1: Part1.D12_PWM, LCD1.RS
  N2: Part1.D11_PWM, LCD1.E
  VDD: Part1.5V, LCD1.VDD, R1.leg1, LCD2.VDD, R2.Pin_1, RHT1.Vcc
  VSS: Part1.GND, LCD1.VSS, LCD1.R/W, LCD1.LED-, R1.leg2, LCD2.VSS, LCD2.R/W, R3.leg2, SPKR1.pin1, RHT1.GND_1
  N3: Part1.D3_PWM, SPKR1.pin2
  N4: Part1.D5_PWM, RHT1.Data-signal
  N5: Part1.D32, LCD2.DB4
  N6: Part1.D33, LCD1.DB4
  N7: Part1.D34, LCD2.DB5
  N8: Part1.D35, LCD1.DB5
  N9: Part1.D36, LCD2.DB6
  N10: Part1.D37, LCD1.DB6
  N11: Part1.D38, LCD2.DB7
  N12: Part1.D39, LCD1.DB7
  N13: Part1.D50, LCD2.RS
  N14: Part1.D52, LCD2.E
  N15: LCD1.V0, R1.wiper
  N16: LCD1.LED+, R2.Pin_0
  N17: LCD2.V0, R3.wiper
